# Fritzing sketch fridge-alarm-fritzing (saved by Fritzing 0.7.10b)
breadboards: 1

parts:
  Arduino1 = Arduino
  LED1 = Red LED - 5mm [package="5 mm [THT]"]
  J1 = Piezo Speaker
  U1 = mystery part, 3 pins [chip_label="Hall Effect Sensor" spacing=300mil]

nets:
  N1: Arduino1.GND, LED1.cathode, J1.pin1, U1.pin2
  N2: Arduino1.D13, LED1.anode
  N3: Arduino1.D8, J1.pin2
  N4: Arduino1.D1TX, U1.pin3
  N5: Arduino1.+5V, U1.pin1
